# Fritzing sketch lettre (saved by Fritzing 0.9.3b)

parts:
  WeMos_D1_Mini1 = WeMos D1 Mini
  R1 = Resistor [tolerance=±5% resistance=220 package="2512 [SMD]"]
  R2 = Photocell (LDR) [package=THT]
  Composant1 = HX711 Weighing Sensor Module
  LED1 = smd LED [color="Red (633nm)" package="0805 [SMD]"]

nets:
  3V3: WeMos_D1_Mini1.3V3, Composant1.VCC
  N1: WeMos_D1_Mini1.A0, R1.Pin_1, R2.pin_1
  N2: WeMos_D1_Mini1.D1, LED1.cathode
  N3: WeMos_D1_Mini1.D2, R2.pin_0
  N4: WeMos_D1_Mini1.D5, Composant1.DO/RX
  N5: WeMos_D1_Mini1.D6, Composant1.CK/TX
  N6: WeMos_D1_Mini1.G, R1.Pin_0, Composant1.GND, LED1.anode
